# Fritzing sketch FM_Receiver (saved by Fritzing 0.9.6b)
breadboards: 1

parts:
  Part1 = Arduino Nano (Rev3.0)
  Part3 = LilyPad Button Board
  R1 = Resistor [tolerance=±5% resistance=10k package="0402 [SMD]"]
  R2 = Resistor [tolerance=±5% resistance=10k package="0402 [SMD]"]
  Grove1 = Grove OLED 128x96
  Part2 = LilyPad Button Board
  IC1 = Dual Op-Amp [package=so08]
  AMP1 = GF1002 Stereo Amplifier
  TRS1 = Audio Jack (TRS) 3.5mm [package="4Ucon 08780 [THT]"]
  SP1 = SPEAKER [package=pcb_mount_speaker]

nets:
  GND: Part1.GND, Part3.-, Grove1.GND, Part2.-, IC1.B_+IN, AMP1.ROUT-, AMP1.LOUT-, AMP1.POWER-, AMP1.INPUTG, TRS1.Sleeve, SP1.+
  N1: Part1.D3, R2.Pin_1, Part2.S
  N2: Part1.D4, Part3.S, R1.Pin_1
  5V: Part1.5V, R1.Pin_0, R2.Pin_0, Grove1.VCC
  N3: Part1.A5, Grove1.SCL, IC1.A_-IN
  N4: Part1.A4, Grove1.SDA, IC1.A_OUT
  N5: Part1.3V3, IC1.A_V-
  N6: IC1.B_-IN, AMP1.LOUT+, TRS1.Ring
  N7: IC1.B_OUT, AMP1.ROUT+, TRS1.Tip
  N8: AMP1.INPUTR, SP1.-

notes:
  FM chip RRD102v2
  Antenna
  Frequency UP and DOWN buttons

custom parts:
  GF1002 Stereo Amplifier: GF1002 6 Watt Stereo Amplifier
